# Fritzing sketch Project_Controller (saved by Fritzing 0.9.10b)
breadboards: 1

parts:
  U1 = ESP32-38PinWide [part_number=ESP32-38PinWide]
  U2 = LoRaWAN RN2483/RN2903 Breakout board
  S1 = Pushbutton [package="[THT]"]
  Part2 = LCD1602-I2C
  R1 = Resistor [tolerance=±5% resistance=10000 package="2010 [SMD]"]
  Mod1 = KY-023 Dual Axis Joystick Module [package="Breakout board"]

nets:
  3V3: U1.3.3, U2.3V3, S1.Pin_3, S1.Pin_4, Part2.VCC, Mod1.+5V
  N1: U1.GPIO34, Mod1.VRy
  N2: U1.GPIO35, Mod1.VRx
  GND: U1.GND, U2.GND, Part2.GND, R1.Pin_1, Mod1.GND
  N3: U1.GPIO4, S1.Pin_1, S1.Pin_2, R1.Pin_0
  N4: U1.GPIO16, U2.TX
  N5: U1.GPIO17, U2.RX
  N6: U1.GPIO21, Part2.SDA
  N7: U1.GPIO22, Part2.SCL
  N8: U1.GPIO23, U2.RTS

custom parts:
  ESP32-38PinWide: Generic 38-Pin ESP32 with wide format (only access to one side of pins on a breadboard) based on Stephen Lilley's HiLetgo ESP-WROOM-32 ESP32 ESP-32S Development Board.
  LoRaWAN RN2483/RN2903 Breakout board: This breakout board offers an affordable solution for makers working with the popular RN2483A and RN2903A LoRa transceivers from Microchip, widely used for LoRaWAN (Commonly called just RN2483 and RN2903, or collectively, RN2xx3). The layout of this breakout board is based on the the datasheet reference designs. This board breaks out all 14 GPIO pins to a row of 0.1" pin header, and the power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
  LCD1602-I2C: A standard character display, usually with 2x16 characters. Comes in many colors with LCM1602 IIC attached.
  KY-023 Dual Axis Joystick Module: KY-023 Dual-Axis Joystick Module.
